# Fritzing sketch Untitled Sketch (saved by Fritzing 0.9.3b)
breadboards: 1

parts:
  Part1 = Arduino Uno (Rev3)
  Part2 = Soil Moisture Sensor
  R1 = Photocell (LDR) [package=THT]
  R2 = Resistor [tolerance=±5% resistance=220 package=THT]

nets:
  N1: Part1.A0, Part2.SIG
  N2: Part1.A1, R2.Pin_0
  GND: Part1.GND, Part2.GND, R2.Pin_1
  5V: Part1.5V, Part2.VCC, R1.pin_1
