# Fritzing sketch Untitled Sketchlatest (saved by Fritzing 0.9.3b)
breadboards: 1

parts:
  Part1 = Arduino Uno (Rev3)
  Part2 = Soil Moisture Sensor
  R1 = Photocell (LDR) [package=THT]
  U1 = TEMPERATURE-SENSOR [package=to-92]

nets:
  N1: Part1.A0, Part2.SIG
  N2: Part1.A1, R1.pin_0
  N3: Part1.A2, U1.ADJ
  GND: Part1.GND, Part2.GND, U1.GND
  VCC: Part1.5V, Part2.VCC, R1.pin_1, U1.VCC
